# Fritzing sketch Circuit Schematic (saved by Fritzing 0.9.4)
breadboards: 1

parts:
  J1 = Basic Force Sensing Resistor (FSR) [package=THT]
  R1 = Resistor [tolerance=±5% resistance=10k package="2512 [SMD]"]
  VCC1 = Battery block 9V
  SG1 = Buzzer 12mm [package=buzzer-ccv]
  Pipette_Tip_Box_Alarm_-_Kzra_2021_(C) = Arduino Nano (Rev3.0)

nets:
  N1: J1.pin_0, Pipette_Tip_Box_Alarm_-_Kzra_2021_(C).5V
  N2: J1.pin_1, Pipette_Tip_Box_Alarm_-_Kzra_2021_(C).A0
  N3: R1.Pin_1, VCC1.-, SG1.2, Pipette_Tip_Box_Alarm_-_Kzra_2021_(C).GND
  N4: VCC1.+, Pipette_Tip_Box_Alarm_-_Kzra_2021_(C).VIN
  N5: SG1.1, Pipette_Tip_Box_Alarm_-_Kzra_2021_(C).D6
